// Logisim project Template.circ as structural Verilog: 2 circuits, main circuit main
module main (
);

  wire clk;

  // Text text_1: pin names not known
  // Text text_2: pin names not known
  // Text text_3: pin names not known
  // Text text_4: pin names not known
  // Text text_5: pin names not known
  Clock #(.highDuration(4), .lowDuration(4)) u_clk (.out(clk));
  Clock sysclk ();  // open: out

  // Notes on the sheet:
  //   LABO ARO 2 - FETCH
  //   HEIG-VD / Institut REDS
  //   Date : 25.02.2014
  //   Ne pas modifier les noms des clocks
endmodule

module PCINC_16BITS (
  input  CLR,
  output [15:0] out_2
);

  wire clock_1_out;
  wire [15:0] adder_1_out, PC_q;

  // Text text_1: pin names not known
  // Text text_2: pin names not known
  // Text text_3: pin names not known
  // Text text_4: pin names not known
  // Text text_5: pin names not known
  Adder #(.width(16)) adder_1 (.a(PC_q), .b(16'h2), .out(adder_1_out));  // open: cin, cout
  Clock #(.highDuration(4), .lowDuration(4)) clock_1 (.out(clock_1_out));
  Register #(.width(16)) PC (.D(adder_1_out), .clk(clock_1_out), .Q(PC_q), .clr(CLR));  // open: en
  ROM #(.addrWidth(16), .dataWidth(16)) MEM_INSTRU (.addr(PC_q), .data(out_2));

  // Notes on the sheet:
  //   contents of MEM_INSTRU (hex, n*v repeats v):
  //   2000 188b
endmodule
